// Logisim project Magic1_Top.circ as structural Verilog: 1 circuit, main circuit Magic1
module Magic1 (
);

  wire front_panel_1_p11, front_panel_1_p13, front_panel_1_p17, front_panel_1_p18, front_panel_1_p19,
       front_panel_1_p20, front_panel_1_p21, front_panel_1_p22, front_panel_1_p24, front_panel_1_p25,
       front_panel_1_p26, front_panel_1_p27, front_panel_1_p28, front_panel_1_p29, front_panel_1_p30,
       front_panel_1_p32, front_panel_1_p34, front_panel_1_p35, front_panel_1_p36, front_panel_1_p37,
       front_panel_1_p38, front_panel_1_p39, front_panel_1_p40, front_panel_1_p41, front_panel_1_p42,
       ic_74138_1_y4, ir_decode_1_p4, ir_decode_1_p12, ir_decode_1_p13, ir_decode_1_p14, ir_decode_1_p15,
       ir_decode_1_p17, ir_decode_1_p20, ir_decode_1_p26, ir_decode_1_p34, nand_1_out, not_1_out, not_2_out,
       U3C_out, U5B_out, U5D_out, U26A_out, U26B_out, U27A_out;
  wire [5:0] front_panel_1_p9;
  wire [7:0] front_panel_1_p4, front_panel_1_p23, ir_decode_1_p11, register_1_q;
  wire [21:0] front_panel_1_p31;

  Register #(.trigger("low")) register_1 (
    .D(front_panel_1_p23), .en(1'b1), .clk(U5B_out), .Q(register_1_q));  // open: clr
  Hex_Digit_Display hex_digit_display_1 (.value(register_1_q[7:4]));  // open: dp
  Hex_Digit_Display hex_digit_display_2 (.value(register_1_q[3:0]));  // open: dp
  or U5B (U5B_out, front_panel_1_p30, ic_74138_1_y4);
  not not_1 (not_1_out, U5B_out);
  // Front_Panel front_panel_1: pin names not known; wires that end beside it: front_panel_1_p9[5], front_panel_1_p9[4], front_panel_1_p9[3], front_panel_1_p4[0], front_panel_1_p9[2], front_panel_1_p4[1], front_panel_1_p9[1], front_panel_1_p4[3], front_panel_1_p9[0], front_panel_1_p4[4], front_panel_1_p11, front_panel_1_p4[6], front_panel_1_p13, front_panel_1_p4[5], 1'b1, front_panel_1_p4[7], front_panel_1_p17, front_panel_1_p18, front_panel_1_p19, front_panel_1_p20, front_panel_1_p21, front_panel_1_p22, front_panel_1_p23, front_panel_1_p24, front_panel_1_p25, front_panel_1_p26, front_panel_1_p27, front_panel_1_p28, front_panel_1_p29, front_panel_1_p30, front_panel_1_p31, front_panel_1_p32, not_1_out, front_panel_1_p34, front_panel_1_p35, front_panel_1_p36, front_panel_1_p37, front_panel_1_p38, front_panel_1_p39, front_panel_1_p40, front_panel_1_p41, front_panel_1_p42
  or U5D (U5D_out, front_panel_1_p17, ir_decode_1_p34);
  // IR_DECODE ir_decode_1: pin names not known; wires that end beside it: front_panel_1_p34, front_panel_1_p35, front_panel_1_p9, ir_decode_1_p4, front_panel_1_p38, front_panel_1_p39, front_panel_1_p25, front_panel_1_p40, front_panel_1_p41, front_panel_1_p42, ir_decode_1_p11, ir_decode_1_p12, ir_decode_1_p13, ir_decode_1_p14, ir_decode_1_p15, front_panel_1_p31, ir_decode_1_p17, front_panel_1_p37, front_panel_1_p30, ir_decode_1_p20, front_panel_1_p19, front_panel_1_p4, front_panel_1_p32, front_panel_1_p22, front_panel_1_p20, ir_decode_1_p26, front_panel_1_p27, front_panel_1_p26, front_panel_1_p28, front_panel_1_p13, front_panel_1_p24, front_panel_1_p29, front_panel_1_p17, ir_decode_1_p34
  RAM_ROM ram_rom_1 (
    .nWE(front_panel_1_p30), .A(front_panel_1_p31), .nOE(U5D_out), .FP_RAM(front_panel_1_p36),
    .MEMORY(front_panel_1_p37), .DBUS(ir_decode_1_p11));
  // REGS regs_1: pin names not known; wires that end beside it: ir_decode_1_p26, ir_decode_1_p17, ir_decode_1_p14, ir_decode_1_p12, front_panel_1_p29, front_panel_1_p17, ir_decode_1_p13, front_panel_1_p13, ir_decode_1_p20, front_panel_1_p21, front_panel_1_p19, front_panel_1_p11, ir_decode_1_p11, front_panel_1_p23, ir_decode_1_p4, ir_decode_1_p15, front_panel_1_p25
  nor U26A (U26A_out, front_panel_1_p31[0], front_panel_1_p31[1], front_panel_1_p31[2]);
  nor U26B (U26B_out, front_panel_1_p31[3], front_panel_1_p31[4], front_panel_1_p31[5]);
  nand nand_1 (nand_1_out, front_panel_1_p31[6], front_panel_1_p31[7], front_panel_1_p31[8], front_panel_1_p31[9], front_panel_1_p31[10], front_panel_1_p31[11], front_panel_1_p31[12], front_panel_1_p31[13], front_panel_1_p31[14]);
  nand U27A (U27A_out, U26A_out, U26B_out);
  nor U3C (U3C_out, U27A_out, nand_1_out, front_panel_1_p37);
  not not_2 (not_2_out, front_panel_1_p28);
  IC_74138 ic_74138_1 (
    .Y2(front_panel_1_p18), .Y4(ic_74138_1_y4), .A2(front_panel_1_p31[15]), .A0(front_panel_1_p31[17]),
    .OE1(not_2_out), .OE2(not_2_out), .OE3(U3C_out), .A1(front_panel_1_p31[16]));  // open: Y0, Y1, Y3, Y5, Y6, Y7
endmodule
